# Fritzing sketch Pflanzenwächter_Schematic_Teil3 (saved by Fritzing 0.9.3b)
breadboards: 2

parts:
  U1 = ESP32-38PinWide [part_number=ESP32-38PinWide]
  YwRobot_Power_Supply1 = YwRobot Breadboard Power Supply [part_number=545043]  # not connected
  R1 = Resistor [tolerance=±1% resistance=130k package=THT]  # not connected
  R2 = Resistor [tolerance=±1% resistance=130k package=THT]  # not connected
  R3 = Resistor [tolerance=±1% resistance=130k package=THT]  # not connected
  R5 = Resistor [tolerance=±1% resistance=130k package=THT]
  R6 = Resistor [tolerance=±1% resistance=130k package=THT]
  R7 = Resistor [tolerance=±1% resistance=47k package=THT]  # not connected
  R8 = Resistor [tolerance=±1% resistance=47k package=THT]
  R9 = Resistor [tolerance=±1% resistance=47k package=THT]  # not connected
  R10 = Resistor [tolerance=±1% resistance=47k package=THT]  # not connected
  R11 = Resistor [tolerance=±1% resistance=130k package=THT]
  R13 = Resistor [tolerance=±1% resistance=47k package=THT]
  SENS1 = SoilWatch 10
  SENS2 = SoilWatch 10
  R14 = Resistor [tolerance=±1% resistance=150 package=THT]
  LED1 = LED - 5mm [color="Green (560nm)" package="5 mm [THT]"]
  LED2 = LED - 5mm [color="Orange (605nm)" package="5 mm [THT]"]
  LED3 = LED - 5mm [color="Red (633nm)" package="5 mm [THT]"]
  R15 = Resistor [tolerance=±1% resistance=150 package=THT]
  R16 = Resistor [tolerance=±1% resistance=150 package=THT]
  SENS3 = SoilWatch 10
  SENS4 = SoilWatch 10
  SENS5 = SoilWatch 10
  SENS6 = SoilWatch 10
  R17 = Resistor [tolerance=±1% resistance=47k package=THT]

nets:
  N1: U1.GPIO15, LED1.cathode
  N2: U1.GPIO18, LED3.cathode
  GND: R5.Pin_1, R6.Pin_1, R11.Pin_1, SENS1.GND, SENS2.GND, SENS3.GND, SENS4.GND, SENS5.GND, SENS6.GND
  N3: R6.Pin_0, R13.Pin_1
  N4: R8.Pin_1, SENS2.OUT
  N5: R11.Pin_0, R17.Pin_1
  N6: R13.Pin_0, SENS5.OUT
  VCC: SENS1.VCC, SENS2.VCC, SENS3.VCC, SENS4.VCC, SENS5.VCC, SENS6.VCC
  N7: R14.Pin_0, R15.Pin_0, R16.Pin_0
  N8: R14.Pin_1, LED2.anode
  N9: LED1.anode, R16.Pin_1
  N10: LED3.anode, R15.Pin_1
  N11: SENS6.OUT, R17.Pin_0

custom parts:
  ESP32-38PinWide: Generic 38-Pin ESP32 with wide format (only access to one side of pins on a breadboard) based on Stephen Lilley's HiLetgo ESP-WROOM-32 ESP32 ESP-32S Development Board.
  YwRobot Breadboard Power Supply: The YwRobot Breadboard Power Supply (MB-V2) has two power rails; they can be 5V or 3V3. Power to the module can be provided through the female USB socket or through the A10 (female) 2.1mm power jack.
  SoilWatch 10: SoilWatch 10 - Capacitive soil moisture sensor
