# Fritzing sketch Pflanzenwächter_Schematic_Teil5 (saved by Fritzing 0.9.3b)
breadboards: 2

parts:
  U1 = ESP32-38PinWide [part_number=ESP32-38PinWide]
  YwRobot_Power_Supply1 = YwRobot Breadboard Power Supply [part_number=545043]  # not connected
  R1 = Resistor [tolerance=±1% resistance=130k package=THT]  # not connected
  R2 = Resistor [tolerance=±1% resistance=130k package=THT]  # not connected
  R3 = Resistor [tolerance=±1% resistance=130k package=THT]  # not connected
  R5 = Resistor [tolerance=±1% resistance=130k package=THT]
  R6 = Resistor [tolerance=±1% resistance=130k package=THT]
  R7 = Resistor [tolerance=±1% resistance=47k package=THT]  # not connected
  R8 = Resistor [tolerance=±1% resistance=47k package=THT]
  R9 = Resistor [tolerance=±1% resistance=47k package=THT]  # not connected
  R10 = Resistor [tolerance=±1% resistance=47k package=THT]  # not connected
  R11 = Resistor [tolerance=±1% resistance=130k package=THT]
  R13 = Resistor [tolerance=±1% resistance=47k package=THT]
  SENS1 = SoilWatch 10
  SENS2 = SoilWatch 10
  SENS3 = SoilWatch 10
  SENS4 = SoilWatch 10
  SENS5 = SoilWatch 10
  SENS6 = SoilWatch 10
  R17 = Resistor [tolerance=±1% resistance=47k package=THT]
  DHT-22_Module1 = DHT-22 Module
  Part1 = KY-016 RGB Full Color LED Module [package="Breakout board"]
  Bauteil2 = BH1750

nets:
  N1: U1.GPIO15, Part1.G
  N2: U1.GPIO0, Part1.R
  N3: U1.GPIO4, DHT-22_Module1.OUT
  N4: U1.GPIO21, Bauteil2.SDA
  N5: U1.GPIO22, Bauteil2.SCL
  GND: R5.Pin_1, R6.Pin_1, R11.Pin_1, SENS1.GND, SENS2.GND, SENS3.GND, SENS4.GND, SENS5.GND, SENS6.GND
  N6: R6.Pin_0, R13.Pin_1
  N7: R8.Pin_1, SENS2.OUT
  N8: R11.Pin_0, R17.Pin_1
  N9: R13.Pin_0, SENS5.OUT
  VCC: SENS1.VCC, SENS2.VCC, SENS3.VCC, SENS4.VCC, SENS5.VCC, SENS6.VCC
  N10: SENS6.OUT, R17.Pin_0
  N11: DHT-22_Module1.+, Bauteil2.VCC
  N12: DHT-22_Module1.-, Part1.-, Bauteil2.GND, Bauteil2.ADDR

custom parts:
  ESP32-38PinWide: Generic 38-Pin ESP32 with wide format (only access to one side of pins on a breadboard) based on Stephen Lilley's HiLetgo ESP-WROOM-32 ESP32 ESP-32S Development Board.
  YwRobot Breadboard Power Supply: The YwRobot Breadboard Power Supply (MB-V2) has two power rails; they can be 5V or 3V3. Power to the module can be provided through the female USB socket or through the A10 (female) 2.1mm power jack.
  SoilWatch 10: SoilWatch 10 - Capacitive soil moisture sensor
  DHT-22 Module: The DHT22 is a reliable Sensor for determining the temperature and humidity. Since the Sensor can be operated both 3,3 V and 5V, suitable for connection to all popular Boards such as Arduino, RN-Control, Raspberry Pi and all other microcontrollers. In addition to the operating voltage, only one Port needs to be used with the Sensor to connect. The output is a serial digital bit string. Thus,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
  KY-016 RGB Full Color LED Module: KY-016 Arduino full color 5mm RGB LED, different colors can be obtained by mixing the three primary colors.
  BH1750: Light Sensor
